# Fritzing sketch wlanthermo_easy (saved by Fritzing 0.9.4)
stripboards: 2

parts:
  R1 = Resistor [tolerance=±20% resistance=1k package=THT]
  R2 = Resistor [tolerance=±20% resistance=47k package=THT]
  R3 = Resistor [tolerance=±20% resistance=47k package=THT]
  R4 = Resistor [tolerance=±20% resistance=1k package=THT]
  U4 = 2.5mm Audio Jack [package=stereojack2.5mm_smd]
  R5 = Resistor [tolerance=±20% resistance=47k package=THT]
  R6 = Resistor [tolerance=±20% resistance=1k package=THT]
  U5 = 2.5mm Audio Jack [package=stereojack2.5mm_smd]
  R7 = Resistor [tolerance=±20% resistance=47k package=THT]
  R8 = Resistor [tolerance=±20% resistance=1k package=THT]
  U1 = NodeMCU V1.0
  Squix1 = OLED 0.96" 128x64 I2C SSD1306
  IC1 = LM4040 [package=to-92]
  MCP1 = MCP3208
  U2 = 2.5mm Audio Jack [package=stereojack2.5mm_smd]
  C1 = Film/Foil Capacitor [capacitance=100nF voltage=35V package="5mm [THT, pp]"]
  C4 = Film/Foil Capacitor [capacitance=100nF voltage=35V package="5mm [THT, pp]"]
  C3 = Film/Foil Capacitor [capacitance=100nF voltage=35V package="5mm [THT, pp]"]
  C2 = Film/Foil Capacitor [capacitance=100nF voltage=35V package="5mm [THT, pp]"]
  C6 = Film/Foil Capacitor [capacitance=100nF voltage=35V package="5mm [THT, pp]"]
  C5 = Film/Foil Capacitor [capacitance=100nF voltage=35V package="5mm [THT, pp]"]
  U3 = 2.5mm Audio Jack [package=stereojack2.5mm_smd]
  R12 = Resistor [tolerance=±20% resistance=10k package=THT]
  R13 = Resistor [tolerance=±20% resistance=10k package=THT]
  S1 = Pushbutton [package=THT]  # not connected
  R14 = Vertical Resistor [tolerance=±5% resistance=2.32k package=THT]
  C7 = Film/Foil Capacitor [capacitance=100nF voltage=35V package="5mm [THT, pp]"]

nets:
  NTC3: R1.Pin_0, MCP1.Chan_4, C1.-
  N1: R1.Pin_1, R2.Pin_1, U2.LEFT
  VRef: R2.Pin_0, R3.Pin_0, R5.Pin_0, R7.Pin_0, IC1.+, MCP1.VREF, R14.Pin_1, C7.-
  N2: R3.Pin_1, R4.Pin_1, U3.LEFT
  NTC4: R4.Pin_0, MCP1.Chan_5, C2.-
  N3: U4.LEFT, R5.Pin_1, R6.Pin_1
  CH12: U4.RIGHT
  GND: U4.SLEEVE, U5.SLEEVE, U1.GND, Squix1.GND, IC1.-, MCP1.DGND, MCP1.AGND, U2.SLEEVE, C1.+, C4.+, C3.+, C2.+, C6.+, C5.+, U3.SLEEVE, C7.+
  NTC5: R6.Pin_0, MCP1.Chan_6, C3.-
  N4: U5.LEFT, R7.Pin_1, R8.Pin_1
  CH11: U5.RIGHT
  NTC6: R8.Pin_0, MCP1.Chan_7, C4.-
  SDA: U1.D0, Squix1.SCA, R13.Pin_0
  SCL: U1.D1, Squix1.SCL, R12.Pin_0
  3.3V: U1.3V3, U1.Vin, Squix1.VCC, MCP1.VDD, C6.-, C5.-, R12.Pin_1, R13.Pin_1, R14.Pin_0
  SCLK: U1.D5, MCP1.CLK
  MISO: U1.D6, MCP1.DOUT
  MOSI: U1.D7, MCP1.DIN
  CS: U1.D8, MCP1.CS/SHDN
  CH9: U2.RIGHT
  CH10: U3.RIGHT

custom parts:
  NodeMCU V1.0: ESP8266 based NodeMCU
  LM4040: Voltage Regulator Standard 7805 5V regulator. IGO (Input Ground Output). Spark Fun Electronics SKU : COM-00107
  Vertical Resistor: A generic resistor (0.25W)
